# Fritzing sketch scheme (saved by Fritzing 0.9.9b)
breadboards: 1

parts:
  U1 = Telaire T6703
  U2 = LuaNode32_ESP32_r1 [part_number=ESP32S-PIN30]

nets:
  N1: U1.connector1, U2.connector6
  N2: U1.connector2, U2.connector5
  N3: U1.connector3, U2.connector14
  N4: U1.connector4, U1.connector6, U2.connector13
