# Fritzing sketch scheme (saved by Fritzing 0.9.9b)
breadboards: 1

parts:
  U2 = NodeMCU V1.0
  U1 = T6703

nets:
  N1: U2.D1, U1.SCL
  N2: U2.D2, U1.SDA
  GND: U2.GND, U1.GND, U1.SEL
  N3: U2.Vin, U1.V+

custom parts:
  NodeMCU V1.0: ESP8266 based NodeMCU
  T6703: Telaire CO2 sensor
